// Logisim project ShiftyCPU.circ as structural Verilog: 4 circuits, main circuit main
module main (
);

  wire Cl0ck_out, controlunit_1_aluop, controlunit_1_memread, controlunit_1_memwrite, controlunit_1_regwrite,
       controlunit_1_writectrl;
  wire [7:0] adder_1_out, alu_1_result, bit_extender_1_out, multiplexer_1_out, multiplexer_2_out, PC_q,
       ram_1_dout, registerfile_1_regdata1, registerfile_1_regdata2, registerfile_1_storeregdata;
  wire [15:0] InstructionRAM_dout;

  Clock Cl0ck (.out(Cl0ck_out));
  Register PC (.D(adder_1_out), .en(Cl0ck_out), .clk(Cl0ck_out), .Q(PC_q));  // open: clr
  Adder adder_1 (.a(PC_q), .b(8'h1), .out(adder_1_out));  // open: cin, cout
  RAM #(.dataWidth(16)) InstructionRAM (
    .addr(PC_q), .oe(1'b1), .clk(Cl0ck_out), .dout(InstructionRAM_dout));  // open: we, din
  RAM #(.trigger("falling")) ram_1 (
    .addr(alu_1_result), .we(controlunit_1_memwrite), .oe(controlunit_1_memread), .clk(Cl0ck_out),
    .din(registerfile_1_storeregdata), .dout(ram_1_dout));
  assign bit_extender_1_out = {{1{InstructionRAM_dout[6]}}, InstructionRAM_dout[6:0]};  // Bit_Extender bit_extender_1
  ControlUnit controlunit_1 (
    .Opcode(InstructionRAM_dout[15:14]), .RegWrite(controlunit_1_regwrite),
    .MemWrite(controlunit_1_memwrite), .MemRead(controlunit_1_memread), .ALUOp(controlunit_1_aluop),
    .WriteCtrl(controlunit_1_writectrl));
  Multiplexer #(.width(8)) multiplexer_1 (
    .in0(bit_extender_1_out), .in1(registerfile_1_regdata2), .out(multiplexer_1_out),
    .sel(InstructionRAM_dout[7]));
  Multiplexer #(.width(8)) multiplexer_2 (
    .in0(alu_1_result), .in1(ram_1_dout), .out(multiplexer_2_out), .sel(controlunit_1_writectrl));
  RegisterFile registerfile_1 (
    .ReadReg1(InstructionRAM_dout[11:10]), .WriteReg(InstructionRAM_dout[13:12]),
    .RegWrite(controlunit_1_regwrite), .RegDataW(multiplexer_2_out), .ReadReg2(InstructionRAM_dout[9:8]),
    .StoreReg(InstructionRAM_dout[13:12]), .Cl0ck(Cl0ck_out), .RegData1(registerfile_1_regdata1),
    .RegData2(registerfile_1_regdata2), .StoreRegData(registerfile_1_storeregdata));
  ALU alu_1 (
    .Val1(registerfile_1_regdata1), .Val2(multiplexer_1_out), .ALUOp(controlunit_1_aluop),
    .Result(alu_1_result));

  // Notes on the sheet:
  //   Jonathan Pruchansky
  //   Arin Ravindran
  //   Shifty CPU
  //   I pledge my honor that I have abided by the Stevens Honor System.
endmodule

module ControlUnit (
  input  [1:0] Opcode,
  output RegWrite,
  output MemWrite,
  output MemRead,
  output ALUOp,
  output WriteCtrl
);

  wire not_1_out, not_2_out, not_3_out, not_4_out, not_5_out, not_6_out;

  not not_1 (not_1_out, Opcode[0]);
  not not_2 (not_2_out, Opcode[1]);
  not not_3 (not_3_out, Opcode[0]);
  not not_4 (not_4_out, Opcode[1]);
  not not_5 (not_5_out, Opcode[0]);
  not not_6 (not_6_out, Opcode[1]);
  or or_1 (RegWrite, not_1_out, Opcode[1]);
  and and_1 (MemWrite, Opcode[0], not_2_out);
  and and_2 (MemRead, not_3_out, not_4_out);
  and and_3 (ALUOp, Opcode[0], Opcode[1]);
  and and_4 (WriteCtrl, not_5_out, not_6_out);

  // Notes on the sheet:
  //   Load - 00
  //   Store - 01
  //   Add - 10
  //   Subtract - 11
  //   ALU OPERATIONS
  //   Add - 0
  //   Subtract - 1
  //   WriteCtrl
  //   0 - Write ALUOut to Register
  //   1 - Write Data from RAM to Register
endmodule

module RegisterFile (
  input  [1:0] ReadReg1,
  input  [1:0] WriteReg,
  input  RegWrite,
  input  [7:0] RegDataW,
  input  [1:0] ReadReg2,
  input  [1:0] StoreReg,
  input  Cl0ck,
  output [7:0] RegData1,
  output [7:0] RegData2,
  output [7:0] StoreRegData
);

  wire and_1_out, and_2_out, and_3_out, and_4_out, decoder_1_out0, decoder_1_out1, decoder_1_out2,
       decoder_1_out3;
  wire [7:0] A_q, B_q, C_q, D_q;

  Decoder #(.select(2)) decoder_1 (
    .out0(decoder_1_out0), .out1(decoder_1_out1), .out2(decoder_1_out2), .out3(decoder_1_out3), .sel(WriteReg));  // open: en
  Register A (.D(RegDataW), .en(and_1_out), .clk(Cl0ck), .Q(A_q));  // open: clr
  and and_1 (and_1_out, decoder_1_out3, RegWrite);
  Register B (.D(RegDataW), .en(and_2_out), .clk(Cl0ck), .Q(B_q));  // open: clr
  and and_2 (and_2_out, decoder_1_out2, RegWrite);
  Register C (.D(RegDataW), .en(and_3_out), .clk(Cl0ck), .Q(C_q));  // open: clr
  and and_3 (and_3_out, decoder_1_out1, RegWrite);
  Register D (.clk(Cl0ck), .Q(D_q), .clr(and_4_out));  // open: D, en
  and and_4 (and_4_out, decoder_1_out0, RegWrite);
  Multiplexer #(.select(2), .width(8)) multiplexer_1 (
    .in0(D_q), .in1(C_q), .in2(B_q), .in3(A_q), .out(RegData1), .sel(ReadReg1));
  Multiplexer #(.select(2), .width(8)) multiplexer_2 (
    .in0(D_q), .in1(C_q), .in2(B_q), .in3(A_q), .out(RegData2), .sel(ReadReg2));
  Multiplexer #(.select(2), .width(8)) multiplexer_3 (
    .in0(D_q), .in1(C_q), .in2(B_q), .in3(A_q), .out(StoreRegData), .sel(StoreReg));

  // Notes on the sheet:
  //   Jonathan Pruchansky
  //   I pledge my honor that I have abided by the Stevens Honor System.
endmodule

module ALU (
  input  [7:0] Val1,
  input  [7:0] Val2,
  input  ALUOp,
  output [7:0] Result
);

  wire [7:0] multiplexer_1_out, negator_1_out;

  Multiplexer #(.width(8)) multiplexer_1 (.in0(Val2), .in1(negator_1_out), .out(multiplexer_1_out), .sel(ALUOp));
  Negator negator_1 (.in(Val2), .out(negator_1_out));
  Adder adder_1 (.a(Val1), .b(multiplexer_1_out), .out(Result));  // open: cin, cout
endmodule
